# Fritzing sketch planTech (saved by Fritzing 1.0.1rc)

parts:
  12_Volt_AC-DC_Adapter_Plug = Power plug
  L298N_Motor_Driver_Module = H-Bridge with L298N
  DOIT_ESP32_DEVKIT_V1_30_PIN = DOIT Esp32 DevKit v1 (30 pins long, 11 pins width) [part_number=ESP32S-PIN30]
  DC-DC_Buck_Converter = LM2596 step down module
  Main_Switch = SWITCH-MOMENTARY-2 [package=tactile-switch-1101ne]
  Pump_Manual_Switch = SWITCH-MOMENTARY-2 [package=tactile-switch-1101ne]
  DHT11_Temperature_and_Humidity_Sensor = KY-015 Temperature & Humidity Sensor Module [package="Breakout board"]
  Capacitive_Soil_Moisture_Sensor = DFRobot Capacitive Soil Moisture Sensor V1.0 [part_number=SEN0193]
  Water_Level_Sensor = Water Level Sensor
  Low_Water_Level_Indicator_LED = LED - 5mm [color="Red (633nm)" current=0.030 package="5 mm [THT]"]
  WATER_PUMP = water pump/motor
  Water_Pump_Activation_LED = DUO LED RG [package="5 mm [THT]"]
  DC-DC_Buck_Converter_2 = LM2596 step down module

nets:
  GND: 12_Volt_AC-DC_Adapter_Plug.GND, L298N_Motor_Driver_Module.GND, DOIT_ESP32_DEVKIT_V1_30_PIN.GND, DC-DC_Buck_Converter.IN-, DC-DC_Buck_Converter.OUT-, DHT11_Temperature_and_Humidity_Sensor.-, Capacitive_Soil_Moisture_Sensor.GND, Water_Level_Sensor.GND, Low_Water_Level_Indicator_LED.cathode, Water_Pump_Activation_LED.common_cathode, DC-DC_Buck_Converter_2.IN-, DC-DC_Buck_Converter_2.OUT-
  N1: 12_Volt_AC-DC_Adapter_Plug.VCC, Main_Switch.1
  N2: L298N_Motor_Driver_Module.12V, Pump_Manual_Switch.2
  N3: L298N_Motor_Driver_Module.IN3, DOIT_ESP32_DEVKIT_V1_30_PIN.D25
  N4: L298N_Motor_Driver_Module.IN4, DOIT_ESP32_DEVKIT_V1_30_PIN.D26
  N5: L298N_Motor_Driver_Module.M2-01, WATER_PUMP.pin_1
  N6: L298N_Motor_Driver_Module.M2-02, WATER_PUMP.pin_2
  N7: DOIT_ESP32_DEVKIT_V1_30_PIN.D2, Low_Water_Level_Indicator_LED.anode
  N8: DOIT_ESP32_DEVKIT_V1_30_PIN.D4, Water_Pump_Activation_LED.green_anode
  N9: DOIT_ESP32_DEVKIT_V1_30_PIN.D34, Capacitive_Soil_Moisture_Sensor.A
  N10: DOIT_ESP32_DEVKIT_V1_30_PIN.D32, Water_Level_Sensor.SIG
  N11: DOIT_ESP32_DEVKIT_V1_30_PIN.D27, DHT11_Temperature_and_Humidity_Sensor.S
  N12: DOIT_ESP32_DEVKIT_V1_30_PIN.VIN, DC-DC_Buck_Converter.OUT+
  N13: DC-DC_Buck_Converter.IN+, Main_Switch.2, Pump_Manual_Switch.1, DC-DC_Buck_Converter_2.IN+
  VCC: DHT11_Temperature_and_Humidity_Sensor.Vin, Capacitive_Soil_Moisture_Sensor.VCC, Water_Level_Sensor.VCC, DC-DC_Buck_Converter_2.OUT+

custom parts:
  H-Bridge with L298N: h-bridge
  DOIT Esp32 DevKit v1 (30 pins long, 11 pins width): The DOIT Esp32 DevKit v1 is one of the development board created by DOIT to evaluate the ESP-WROOM-32 module. It is based on the ESP32 microcontroller that boasts Wifi, Bluetooth, Ethernet and Low Power support all in a single chip. (vanepp) made breadboard work, adjusted pin numbering and labels and reduced size of schematic and cleaned up pcb. This chip is 30pins long (2 x15) and 11 pins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
  LM2596 step down module: LM2596 DC-DC step down power supply module 3 A.
  KY-015 Temperature & Humidity Sensor Module: KY-015 temperature and humidity sensor module, provides a low-latency serial interface to measure humidity and temperature.
  DFRobot Capacitive Soil Moisture Sensor V1.0: DFRobot Capacitive Soil Moisture Sensor V1.0 This product measures soil moisture levels by capacitive sensing, rather than resistive sensing like other types of moisture sensor. It is made of a corrosion resistant material giving it a long service life. Insert it into soil and impress your friends with the real-time soil moisture data! The product includes an on-board voltage regulator which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
  Water Level Sensor: A water level sensor. This sensor operates at 3V to 5V. The Sig (signal) pin outputs an analogue signal that is in proportion to the amount of water in contact with the sensor.
  water pump/motor: WATER PUMP BY ARDUBLOCKTR
